// Logisim project monociclo.circ as structural Verilog: 24 circuits, main circuit main
module main (
  input  Reset
);

  wire alu_1_zero, ALUSrc, and_1_out, Branch, clk, Jr, Jump, Link, MemRead, MemtoReg, MemWrite, RegDst,
       RegWrite;
  wire [1:0] ALUOp;
  wire [2:0] alucontrol_1_op;
  wire [4:0] multiplexer_1_out, multiplexer_2_out;
  wire [5:0] i26_31;
  wire [23:0] division_4_1_o, division_4_2_o;
  wire [25:0] inst;
  wire [27:0] shift_left_2_28_1_out28;
  wire [31:0] adder_2_out, alu_1_aluresult, j_1_out32, multiplexer_3_out, multiplexer_4_out,
       multiplexer_5_out, multiplexer_6_out, multiplexer_7_out, multiplexer_8_out, pc_4, PC_q, ramme_1_dato,
       rs, shift_left_2_1_o32, sign_extend_1_out32, WriteData;

  Clock u_CLK (.out(clk));
  Register #(.width(32)) PC (.D(multiplexer_7_out), .en(1'b1), .clk(clk), .Q(PC_q), .clr(Reset));
  // Probe on PC_q
  // Probe on multiplexer_7_out
  // Probe on division_4_1_o
  division_4 division_4_1 (.i(PC_q), .o(division_4_1_o));
  Control control_1 (
    .OP(i26_31), .RegDst(RegDst), .ALUSrc(ALUSrc), .MemtoReg(MemtoReg), .RegWrite(RegWrite),
    .MemRead(MemRead), .MemWrite(MemWrite), .Branch(Branch), .ALUOp(ALUOp), .Jump(Jump), .Link(Link));
  // Probe on ALUOp
  Adder #(.width(32)) adder_1 (.a(32'h4), .b(PC_q), .out(pc_4));  // open: cin, cout
  // Probe on i26_31
  RomMe romme_1 (.regis(division_4_1_o), .Dato({i26_31, inst}));
  // Probe on inst[15:11]
  Multiplexer #(.width(5), .enable("false")) multiplexer_1 (
    .in0(inst[20:16]), .in1(inst[15:11]), .out(multiplexer_1_out), .sel(RegDst));
  // Probe on inst[20:16]
  Multiplexer #(.width(5), .enable("false")) multiplexer_2 (
    .in0(multiplexer_1_out), .in1({5{1'b1}}), .out(multiplexer_2_out), .sel(Link));
  Shift_left_2_28 shift_left_2_28_1 (.in26(inst), .out28(shift_left_2_28_1_out28));
  Sign_extend sign_extend_1 (.in16(inst[15:0]), .out32(sign_extend_1_out32));
  Jr_decoder jr_decoder_1 (.Op(inst[5:0]), .ALUOp(ALUOp), .jr(Jr));
  J j_1 (.in28(shift_left_2_28_1_out28), .in4(pc_4[31:28]), .out32(j_1_out32));
  Shift_left_2 shift_left_2_1 (.i32(sign_extend_1_out32), .o32(shift_left_2_1_o32));
  Register_Bank register_bank_1 (
    .Read_Reg_1(inst[25:21]), .Read_Reg_2(inst[20:16]), .Write_Reg(multiplexer_2_out),
    .Write_Data(multiplexer_4_out), .RegWrite(RegWrite), .CLK(clk), .Reset(Reset), .Read_Data_1(rs),
    .Read_Data_2(WriteData));
  Multiplexer #(.width(32), .enable("false")) multiplexer_3 (
    .in0(WriteData), .in1(sign_extend_1_out32), .out(multiplexer_3_out), .sel(ALUSrc));
  Adder #(.width(32)) adder_2 (.a(pc_4), .b(shift_left_2_1_o32), .out(adder_2_out));  // open: cin, cout
  // Probe on rs
  // Probe on multiplexer_3_out
  Multiplexer #(.width(32), .enable("false")) multiplexer_4 (
    .in0(multiplexer_8_out), .in1(pc_4), .out(multiplexer_4_out), .sel(Link));
  ALUControl alucontrol_1 (.ALUOp(ALUOp), .Funcion(inst[5:0]), .Op(alucontrol_1_op));
  // Probe on multiplexer_4_out
  and and_1 (and_1_out, Branch, alu_1_zero);
  ALU alu_1 (.a(rs), .b(multiplexer_3_out), .ALUOp(alucontrol_1_op), .ALUResult(alu_1_aluresult), .Zero(alu_1_zero));
  // Probe on alu_1_aluresult
  Multiplexer #(.width(32), .enable("false")) multiplexer_5 (
    .in0(pc_4), .in1(adder_2_out), .out(multiplexer_5_out), .sel(and_1_out));
  Multiplexer #(.width(32), .enable("false")) multiplexer_6 (
    .in0(multiplexer_5_out), .in1(j_1_out32), .out(multiplexer_6_out), .sel(Jump));
  division_4 division_4_2 (.i(alu_1_aluresult), .o(division_4_2_o));
  Multiplexer #(.width(32), .enable("false")) multiplexer_7 (
    .in0(multiplexer_6_out), .in1(rs), .out(multiplexer_7_out), .sel(Jr));
  RamMe ramme_1 (
    .regi(division_4_2_o), .W(MemWrite), .R_W(MemRead), .clk(clk), .W_data(WriteData), .Dato(ramme_1_dato));
  Multiplexer #(.width(32), .enable("false")) multiplexer_8 (
    .in0(alu_1_aluresult), .in1(ramme_1_dato), .out(multiplexer_8_out), .sel(MemtoReg));

  // Other names for the same wires on the sheet: inst[31:26] = i26_31
endmodule

module RamMe (
  input  [23:0] regi,
  input  W,
  input  R_W,
  input  clk,
  input  [31:0] W_data,
  output [31:0] Dato
);

  RAM #(.addrWidth(24), .dataWidth(32), .trigger("falling"), .databus("bibus")) ram_1 (
    .addr(regi), .we(W), .oe(R_W), .clk(clk), .din(W_data), .dout(Dato));
endmodule

module RomMe (
  input  [23:0] regis,
  output [31:0] Dato
);

  ROM #(.addrWidth(24), .dataWidth(32)) rom_1 (.addr(regis), .data(Dato));

  // Notes on the sheet:
  //   contents of rom_1 (hex, n*v repeats v):
  //   4020 8d090000 8d0a0004 c000006 1495020 ad0a0008 1495822 ad0b000c
endmodule

module Register32 (
  input  W1,
  input  W2,
  input  W3,
  input  W4,
  input  W5,
  input  W6,
  input  W7,
  input  W8,
  input  W9,
  input  W10,
  input  W11,
  input  W12,
  input  W13,
  input  W14,
  input  W15,
  input  W16,
  input  W17,
  input  W18,
  input  W19,
  input  W20,
  input  W21,
  input  W22,
  input  W23,
  input  W24,
  input  W25,
  input  W26,
  input  W27,
  input  W28,
  input  W29,
  input  W30,
  input  W31,
  input  [31:0] Write_Data,
  input  CLK,
  input  Reset,
  output [31:0] R0,
  output [31:0] R1,
  output [31:0] R2,
  output [31:0] R3,
  output [31:0] R4,
  output [31:0] R5,
  output [31:0] R6,
  output [31:0] R7,
  output [31:0] R8,
  output [31:0] R9,
  output [31:0] R10,
  output [31:0] R11,
  output [31:0] R12,
  output [31:0] R13,
  output [31:0] R14,
  output [31:0] R15,
  output [31:0] R16,
  output [31:0] R17,
  output [31:0] R18,
  output [31:0] R19,
  output [31:0] R20,
  output [31:0] R21,
  output [31:0] R22,
  output [31:0] R23,
  output [31:0] R24,
  output [31:0] R25,
  output [31:0] R26,
  output [31:0] R27,
  output [31:0] R28,
  output [31:0] R29,
  output [31:0] R30,
  output [31:0] R31
);

  Register #(.width(32)) register_1 (.D({32{1'b0}}), .en(1'b0), .clk(CLK), .Q(R0), .clr(Reset));
  Registers16 registers16_1 (
    .W1(W1), .W2(W2), .W3(W3), .W4(W4), .W5(W5), .W6(W6), .W7(W7), .W8(W8), .W9(W9), .W10(W10), .W11(W11),
    .W12(W12), .W13(W13), .W14(W14), .W15(W15), .W16(W16), .Write_Data(Write_Data), .CLK(CLK), .Reset(Reset),
    .R1(R1), .R2(R2), .R3(R3), .R4(R4), .R5(R5), .R6(R6), .R7(R7), .R8(R8), .R9(R9), .R10(R10), .R11(R11),
    .R12(R12), .R13(R13), .R14(R14), .R15(R15), .R16(R16));
  Registers16 registers16_2 (
    .W1(W17), .W2(W18), .W3(W19), .W4(W20), .W5(W21), .W6(W22), .W7(W23), .W8(W24), .W9(W25), .W10(W26),
    .W11(W27), .W12(W28), .W13(W29), .W14(W30), .W15(W31), .Write_Data(Write_Data), .CLK(CLK), .Reset(Reset),
    .R1(R17), .R2(R18), .R3(R19), .R4(R20), .R5(R21), .R6(R22), .R7(R23), .R8(R24), .R9(R25), .R10(R26),
    .R11(R27), .R12(R28), .R13(R29), .R14(R30), .R15(R31));  // open: W16, R16
endmodule

module Registers_4 (
  input  [31:0] Write_Data,
  input  W1,
  input  W2,
  input  W3,
  input  W4,
  input  CLK,
  input  Reset,
  output [31:0] R1,
  output [31:0] R2,
  output [31:0] R3,
  output [31:0] R4
);

  Register #(.width(32)) register_1 (.D(Write_Data), .en(W1), .clk(CLK), .Q(R1), .clr(Reset));
  Register #(.width(32)) register_2 (.D(Write_Data), .en(W2), .clk(CLK), .Q(R2), .clr(Reset));
  Register #(.width(32)) register_3 (.D(Write_Data), .en(W3), .clk(CLK), .Q(R3), .clr(Reset));
  Register #(.width(32)) register_4 (.D(Write_Data), .en(W4), .clk(CLK), .Q(R4), .clr(Reset));
endmodule

module Registers16 (
  input  W1,
  input  W2,
  input  W3,
  input  W4,
  input  W5,
  input  W6,
  input  W7,
  input  W8,
  input  W9,
  input  W10,
  input  W11,
  input  W12,
  input  W13,
  input  W14,
  input  W15,
  input  W16,
  input  [31:0] Write_Data,
  input  CLK,
  input  Reset,
  output [31:0] R1,
  output [31:0] R2,
  output [31:0] R3,
  output [31:0] R4,
  output [31:0] R5,
  output [31:0] R6,
  output [31:0] R7,
  output [31:0] R8,
  output [31:0] R9,
  output [31:0] R10,
  output [31:0] R11,
  output [31:0] R12,
  output [31:0] R13,
  output [31:0] R14,
  output [31:0] R15,
  output [31:0] R16
);

  Registers_4 registers_4_1 (
    .Write_Data(Write_Data), .W1(W1), .W2(W2), .W3(W3), .W4(W4), .CLK(CLK), .Reset(Reset), .R1(R1), .R2(R2),
    .R3(R3), .R4(R4));
  Registers_4 registers_4_2 (
    .Write_Data(Write_Data), .W1(W5), .W2(W6), .W3(W7), .W4(W8), .CLK(CLK), .Reset(Reset), .R1(R5), .R2(R6),
    .R3(R7), .R4(R8));
  Registers_4 registers_4_3 (
    .Write_Data(Write_Data), .W1(W9), .W2(W10), .W3(W11), .W4(W12), .CLK(CLK), .Reset(Reset), .R1(R9),
    .R2(R10), .R3(R11), .R4(R12));
  Registers_4 registers_4_4 (
    .Write_Data(Write_Data), .W1(W13), .W2(W14), .W3(W15), .W4(W16), .CLK(CLK), .Reset(Reset), .R1(R13),
    .R2(R14), .R3(R15), .R4(R16));
endmodule

module Register_Bank (
  input  [4:0] Read_Reg_1,
  input  [4:0] Read_Reg_2,
  input  [4:0] Write_Reg,
  input  [31:0] Write_Data,
  input  RegWrite,
  input  CLK,
  input  Reset,
  output [31:0] Read_Data_1,
  output [31:0] Read_Data_2
);

  wire decoder_1_out1, decoder_1_out2, decoder_1_out3, decoder_1_out4, decoder_1_out5, decoder_1_out6,
       decoder_1_out7, decoder_1_out8, decoder_1_out9, decoder_1_out10, decoder_1_out11, decoder_1_out12,
       decoder_1_out13, decoder_1_out14, decoder_1_out15, decoder_1_out16, decoder_1_out17, decoder_1_out18,
       decoder_1_out19, decoder_1_out20, decoder_1_out21, decoder_1_out22, decoder_1_out23, decoder_1_out24,
       decoder_1_out25, decoder_1_out26, decoder_1_out27, decoder_1_out28, decoder_1_out29, decoder_1_out30,
       decoder_1_out31;
  wire [31:0] R0, R1, R2, R3, R4, R5, R6, R7, R8, R9, R10, R11, R12, R13, R14, R15, R16, R17, R18, R19, R20,
       R21, R22, R23, R24, R25, R26, R27, R28, R29, R30, R31;

  Decoder #(.select(5)) decoder_1 (
    .out1(decoder_1_out1), .out2(decoder_1_out2), .out3(decoder_1_out3), .out4(decoder_1_out4),
    .out5(decoder_1_out5), .out6(decoder_1_out6), .out7(decoder_1_out7), .out8(decoder_1_out8),
    .out9(decoder_1_out9), .out10(decoder_1_out10), .out11(decoder_1_out11), .out12(decoder_1_out12),
    .out13(decoder_1_out13), .out14(decoder_1_out14), .out15(decoder_1_out15), .out16(decoder_1_out16),
    .out17(decoder_1_out17), .out18(decoder_1_out18), .out19(decoder_1_out19), .out20(decoder_1_out20),
    .out21(decoder_1_out21), .out22(decoder_1_out22), .out23(decoder_1_out23), .out24(decoder_1_out24),
    .out25(decoder_1_out25), .out26(decoder_1_out26), .out27(decoder_1_out27), .out28(decoder_1_out28),
    .out29(decoder_1_out29), .out30(decoder_1_out30), .out31(decoder_1_out31), .sel(Write_Reg), .en(RegWrite));  // open: out0
  Register32 register32_1 (
    .W1(decoder_1_out1), .W2(decoder_1_out2), .W3(decoder_1_out3), .W4(decoder_1_out4), .W5(decoder_1_out5),
    .W6(decoder_1_out6), .W7(decoder_1_out7), .W8(decoder_1_out8), .W9(decoder_1_out9),
    .W10(decoder_1_out10), .W11(decoder_1_out11), .W12(decoder_1_out12), .W13(decoder_1_out13),
    .W14(decoder_1_out14), .W15(decoder_1_out15), .W16(decoder_1_out16), .W17(decoder_1_out17),
    .W18(decoder_1_out18), .W19(decoder_1_out19), .W20(decoder_1_out20), .W21(decoder_1_out21),
    .W22(decoder_1_out22), .W23(decoder_1_out23), .W24(decoder_1_out24), .W25(decoder_1_out25),
    .W26(decoder_1_out26), .W27(decoder_1_out27), .W28(decoder_1_out28), .W29(decoder_1_out29),
    .W30(decoder_1_out30), .W31(decoder_1_out31), .Write_Data(Write_Data), .CLK(CLK), .Reset(Reset), .R0(R0),
    .R1(R1), .R2(R2), .R3(R3), .R4(R4), .R5(R5), .R6(R6), .R7(R7), .R8(R8), .R9(R9), .R10(R10), .R11(R11),
    .R12(R12), .R13(R13), .R14(R14), .R15(R15), .R16(R16), .R17(R17), .R18(R18), .R19(R19), .R20(R20),
    .R21(R21), .R22(R22), .R23(R23), .R24(R24), .R25(R25), .R26(R26), .R27(R27), .R28(R28), .R29(R29),
    .R30(R30), .R31(R31));
  Multiplexer #(.select(5), .width(32), .enable("false")) multiplexer_1 (
    .in0(R0), .in1(R1), .in2(R2), .in3(R3), .in4(R4), .in5(R5), .in6(R6), .in7(R7), .in8(R8), .in9(R9),
    .in10(R10), .in11(R11), .in12(R12), .in13(R13), .in14(R14), .in15(R15), .in16(R16), .in17(R17),
    .in18(R18), .in19(R19), .in20(R20), .in21(R21), .in22(R22), .in23(R23), .in24(R24), .in25(R25),
    .in26(R26), .in27(R27), .in28(R28), .in29(R29), .in30(R30), .in31(R31), .out(Read_Data_1),
    .sel(Read_Reg_1));
  Multiplexer #(.select(5), .width(32), .enable("false")) multiplexer_2 (
    .in0(R0), .in1(R1), .in2(R2), .in3(R3), .in4(R4), .in5(R5), .in6(R6), .in7(R7), .in8(R8), .in9(R9),
    .in10(R10), .in11(R11), .in12(R12), .in13(R13), .in14(R14), .in15(R15), .in16(R16), .in17(R17),
    .in18(R18), .in19(R19), .in20(R20), .in21(R21), .in22(R22), .in23(R23), .in24(R24), .in25(R25),
    .in26(R26), .in27(R27), .in28(R28), .in29(R29), .in30(R30), .in31(R31), .out(Read_Data_2),
    .sel(Read_Reg_2));

  // Other names for the same wires on the sheet: readR1[4:0] = Read_Reg_1; readR2[4:0] = Read_Reg_2
endmodule

module FA_1bit (
  input  A,
  input  B,
  input  Cin,
  output Sum,
  output Cout,
  output Overflow
);

  wire and_1_out, and_2_out, and_3_out, and_4_out, and_5_out, and_6_out, and_7_out, and_8_out, and_9_out,
       not_1_out, not_2_out, not_3_out, not_4_out, not_5_out, not_6_out, not_7_out, not_8_out, not_9_out;

  not not_1 (not_1_out, A);
  not not_2 (not_2_out, B);
  not not_3 (not_3_out, A);
  not not_4 (not_4_out, Cin);
  not not_5 (not_5_out, B);
  not not_6 (not_6_out, Cin);
  and and_1 (and_1_out, A, B);
  and and_2 (and_2_out, A, Cin);
  and and_3 (and_3_out, Cin, B);
  not not_7 (not_7_out, A);
  not not_8 (not_8_out, B);
  not not_9 (not_9_out, Cin);
  and and_4 (and_4_out, not_1_out, not_2_out, Cin);
  and and_5 (and_5_out, not_3_out, B, not_4_out);
  and and_6 (and_6_out, A, not_5_out, not_6_out);
  and and_7 (and_7_out, A, B, Cin);
  and and_8 (and_8_out, not_7_out, not_8_out, Cin);
  and and_9 (and_9_out, A, B, not_9_out);
  or or_1 (Sum, and_4_out, and_5_out, and_6_out, and_7_out);
  or or_2 (Cout, and_1_out, and_2_out, and_3_out);
  or or_3 (Overflow, and_8_out, and_9_out);
endmodule

module ALU_1bit (
  input  a,
  input  b,
  input  [2:0] ALUOp,
  input  Cin,
  input  binv,
  output R,
  output Cout
);

  wire bop, not_1_out, not_2_out, r_add_sub, r_and, r_or;

  not not_1 (not_1_out, b);
  Multiplexer #(.enable("false")) multiplexer_1 (.in0(b), .in1(not_1_out), .out(bop), .sel(binv));
  and and_1 (r_and, a, bop);
  or or_1 (r_or, a, bop);
  FA_1bit fa_1bit_1 (.A(a), .B(bop), .Cin(Cin), .Sum(r_add_sub), .Cout(Cout));  // open: Overflow
  not not_2 (not_2_out, r_or);
  Multiplexer #(.select(3), .enable("false")) multiplexer_2 (
    .in0(1'b0), .in1(r_add_sub), .in2(r_and), .in3(r_or), .in4(r_add_sub), .in5(r_add_sub), .in6(1'b0),
    .in7(not_2_out), .out(R), .sel(ALUOp));
endmodule

module ALU_4bits (
  input  [2:0] ALUOp,
  input  [3:0] a,
  input  [3:0] b,
  input  Cin,
  input  binv,
  output [3:0] R,
  output Cout
);

  wire Cout0, Cout1, Cout2;

  ALU_1bit alu_1bit_1 (.a(a[0]), .b(b[0]), .ALUOp(ALUOp), .Cin(Cin), .binv(binv), .R(R[0]), .Cout(Cout0));
  ALU_1bit alu_1bit_2 (.a(a[1]), .b(b[1]), .ALUOp(ALUOp), .Cin(Cout0), .binv(binv), .R(R[1]), .Cout(Cout1));
  ALU_1bit alu_1bit_3 (.a(a[2]), .b(b[2]), .ALUOp(ALUOp), .Cin(Cout1), .binv(binv), .R(R[2]), .Cout(Cout2));
  ALU_1bit alu_1bit_4 (.a(a[3]), .b(b[3]), .ALUOp(ALUOp), .Cin(Cout2), .binv(binv), .R(R[3]), .Cout(Cout));
endmodule

module ALU_1bitOverFlow (
  input  a,
  input  b,
  input  [2:0] ALUOp,
  input  Cin,
  input  binv,
  output R,
  output Cout,
  output slt
);

  wire bneg, bop, not_2_out, r_add_sub, r_and, r_or;

  not not_1 (bneg, b);
  Multiplexer #(.enable("false")) multiplexer_1 (.in0(b), .in1(bneg), .out(bop), .sel(binv));
  and and_1 (r_and, a, bop);
  or or_1 (r_or, a, bop);
  FA_1bit fa_1bit_1 (.A(a), .B(bop), .Cin(Cin), .Sum(r_add_sub), .Cout(Cout), .Overflow(slt));
  not not_2 (not_2_out, r_or);
  Multiplexer #(.select(3), .enable("false")) multiplexer_2 (
    .in0(1'b0), .in1(r_add_sub), .in2(r_and), .in3(r_or), .in4(r_add_sub), .in5(r_add_sub), .in6(1'b0),
    .in7(not_2_out), .out(R), .sel(ALUOp));
endmodule

module ALU_4OverFlow (
  input  [2:0] ALUOp,
  input  [3:0] a,
  input  [3:0] b,
  input  Cin,
  input  binv,
  output [3:0] R,
  output slt
);

  wire alu_1bitoverflow_1_cout, alu_1bitoverflow_1_slt, Cout0, Cout1, Cout2;

  ALU_1bit alu_1bit_1 (.a(a[0]), .b(b[0]), .ALUOp(ALUOp), .Cin(Cin), .binv(binv), .R(R[0]), .Cout(Cout0));
  ALU_1bit alu_1bit_2 (.a(a[1]), .b(b[1]), .ALUOp(ALUOp), .Cin(Cout0), .binv(binv), .R(R[1]), .Cout(Cout1));
  ALU_1bit alu_1bit_3 (.a(a[2]), .b(b[2]), .ALUOp(ALUOp), .Cin(Cout1), .binv(binv), .R(R[2]), .Cout(Cout2));
  ALU_1bitOverFlow alu_1bitoverflow_1 (
    .a(a[3]), .b(b[3]), .ALUOp(ALUOp), .Cin(Cout2), .binv(binv), .R(R[3]), .Cout(alu_1bitoverflow_1_cout),
    .slt(alu_1bitoverflow_1_slt));
  Multiplexer #(.enable("false")) multiplexer_1 (
    .in0(R[3]), .in1(alu_1bitoverflow_1_cout), .out(slt), .sel(alu_1bitoverflow_1_slt));
endmodule

module ALU_32bits (
  input  [2:0] ALUOp,
  input  [31:0] a,
  input  [31:0] b,
  input  binv,
  output [31:0] R,
  output slt
);

  wire Cout0, Cout1, Cout2, Cout3, Cout4, Cout5, Cout6;

  ALU_4bits alu_4bits_1 (.ALUOp(ALUOp), .a(a[3:0]), .b(b[3:0]), .Cin(binv), .binv(binv), .R(R[3:0]), .Cout(Cout0));
  ALU_4bits alu_4bits_2 (.ALUOp(ALUOp), .a(a[7:4]), .b(b[7:4]), .Cin(Cout0), .binv(binv), .R(R[7:4]), .Cout(Cout1));
  ALU_4bits alu_4bits_3 (.ALUOp(ALUOp), .a(a[11:8]), .b(b[11:8]), .Cin(Cout1), .binv(binv), .R(R[11:8]), .Cout(Cout2));
  ALU_4bits alu_4bits_4 (
    .ALUOp(ALUOp), .a(a[15:12]), .b(b[15:12]), .Cin(Cout2), .binv(binv), .R(R[15:12]), .Cout(Cout3));
  ALU_4bits alu_4bits_5 (
    .ALUOp(ALUOp), .a(a[19:16]), .b(b[19:16]), .Cin(Cout3), .binv(binv), .R(R[19:16]), .Cout(Cout4));
  ALU_4bits alu_4bits_6 (
    .ALUOp(ALUOp), .a(a[23:20]), .b(b[23:20]), .Cin(Cout4), .binv(binv), .R(R[23:20]), .Cout(Cout5));
  ALU_4bits alu_4bits_7 (
    .ALUOp(ALUOp), .a(a[27:24]), .b(b[27:24]), .Cin(Cout5), .binv(binv), .R(R[27:24]), .Cout(Cout6));
  ALU_4OverFlow alu_4overflow_1 (
    .ALUOp(ALUOp), .a(a[31:28]), .b(b[31:28]), .Cin(Cout6), .binv(binv), .R(R[31:28]), .slt(slt));

  // Other names for the same wires on the sheet: a0[3:0] = a[3:0]; a1[3:0] = a[7:4]; a2[3:0] = a[11:8];
  //   a3[3:0] = a[15:12]; a4[3:0] = a[19:16]; a5[3:0] = a[23:20]; a6[3:0] = a[27:24]; a7[3:0] = a[31:28];
  //   b0[3:0] = b[3:0]; b1[3:0] = b[7:4]; b2[3:0] = b[11:8]; b3[3:0] = b[15:12]; b4[3:0] = b[19:16];
  //   b5[3:0] = b[23:20]; b6[3:0] = b[27:24]; b7[3:0] = b[31:28]; ctl[2:0] = ALUOp
endmodule

module ALU (
  input  [31:0] a,
  input  [31:0] b,
  input  [2:0] ALUOp,
  output [31:0] ALUResult,
  output Zero
);

  wire multiplexer_1_out;
  wire [0:0] alu_32bits_1_slt;
  wire [31:0] alu_32bits_1_r;

  Multiplexer #(.select(3), .enable("false")) multiplexer_1 (
    .in0(1'b0), .in1(1'b1), .in2(1'b0), .in3(1'b0), .in4(1'b1), .in5(1'b0), .in6(1'b0), .in7(1'b0),
    .out(multiplexer_1_out), .sel(ALUOp));
  ALU_32bits alu_32bits_1 (
    .ALUOp(ALUOp), .a(a), .b(b), .binv(multiplexer_1_out), .R(alu_32bits_1_r), .slt(alu_32bits_1_slt[0]));
  Multiplexer #(.select(3), .width(32), .enable("false")) multiplexer_2 (
    .in0({32{1'b0}}), .in1(alu_32bits_1_r), .in2(alu_32bits_1_r), .in3(alu_32bits_1_r),
    .in4({{31{1'b0}}, alu_32bits_1_slt[0]}), .in5(alu_32bits_1_r), .in6({32{1'b0}}), .in7(alu_32bits_1_r),
    .out(ALUResult), .sel(ALUOp));
  or or_1 (Zero, ALUResult[0], ALUResult[1], ALUResult[2], ALUResult[3], ALUResult[4], ALUResult[5], ALUResult[6], ALUResult[7], ALUResult[8], ALUResult[9], ALUResult[10], ALUResult[11], ALUResult[12], ALUResult[13], ALUResult[14], ALUResult[15], ALUResult[17], ALUResult[18], ALUResult[19], ALUResult[20], ALUResult[21], ALUResult[22], ALUResult[23], ALUResult[24], ALUResult[25], ALUResult[26], ALUResult[27], ALUResult[28], ALUResult[29], ALUResult[30], ALUResult[31], ALUResult[16]);

  // Other names for the same wires on the sheet: op[2:0] = ALUOp
endmodule

module Control (
  input  [5:0] OP,
  output RegDst,
  output ALUSrc,
  output MemtoReg,
  output RegWrite,
  output MemRead,
  output MemWrite,
  output Branch,
  output [1:0] ALUOp,
  output Jump,
  output Link
);

  wire and_3_out, and_4_out, not_1_out, not_2_out, not_3_out, not_4_out, not_5_out, not_6_out, not_7_out,
       not_8_out, not_9_out, not_10_out, not_11_out, not_12_out;

  not not_1 (not_1_out, OP[3]);
  and and_1 (RegDst, not_1_out, not_2_out);
  not not_2 (not_2_out, OP[1]);
  or or_1 (ALUSrc, OP[1], OP[3]);
  not not_3 (not_3_out, OP[3]);
  and and_2 (MemtoReg, not_3_out, OP[1]);
  not not_4 (not_4_out, OP[2]);
  and and_3 (and_3_out, not_4_out, not_5_out);
  not not_5 (not_5_out, OP[1]);
  not not_6 (not_6_out, OP[3]);
  and and_4 (and_4_out, not_6_out, OP[0]);
  and and_5 (MemRead, OP[5], not_7_out);
  not not_7 (not_7_out, OP[3]);
  and and_6 (MemWrite, OP[5], OP[3]);
  not not_8 (not_8_out, OP[3]);
  and and_7 (ALUOp[1], not_8_out, not_9_out, not_10_out);
  not not_9 (not_9_out, OP[2]);
  not not_10 (not_10_out, OP[1]);
  not not_11 (not_11_out, OP[5]);
  and and_8 (Jump, not_11_out, OP[1]);
  not not_12 (not_12_out, OP[5]);
  and and_9 (Link, not_12_out, OP[0]);
  or or_2 (RegWrite, and_3_out, and_4_out);

  assign ALUOp[0] = OP[2];
  assign Branch = OP[2];
endmodule

module ALUControl (
  input  [1:0] ALUOp,
  input  [5:0] Funcion,
  output [2:0] Op
);

  wire and_1_out, and_2_out, and_3_out, not_1_out, not_2_out, not_3_out, not_4_out;
  wire [2:0] or_2_out;
  wire [2:2] not_5_out;

  not not_1 (not_1_out, Funcion[2]);
  not not_2 (not_2_out, Funcion[1]);
  not not_3 (not_3_out, Funcion[3]);
  not not_4 (not_4_out, Funcion[2]);
  not not_5 (not_5_out[2], ALUOp[0]);
  and and_1 (and_1_out, not_1_out, not_2_out);
  and and_2 (and_2_out, Funcion[2], Funcion[1]);
  and and_3 (and_3_out, not_3_out, not_4_out);
  or or_1 (or_2_out[2], and_1_out, and_2_out, Funcion[3]);
  or or_2 (or_2_out[0], and_3_out, Funcion[0]);
  Multiplexer #(.width(3), .enable("false")) multiplexer_1 (
    .in0({not_5_out[2], 2'b01}), .in1({or_2_out[2], Funcion[2], or_2_out[0]}), .out(Op), .sel(ALUOp[1]));

  // Other names for the same wires on the sheet: F = ALUOp[1]
endmodule

module Jr_decoder (
  input  [5:0] Op,
  input  [1:0] ALUOp,
  output jr
);

  wire and_1_out, and_2_out, not_1_out, not_2_out, not_3_out, not_4_out, not_5_out, not_6_out;

  not not_1 (not_1_out, Op[0]);
  not not_2 (not_2_out, Op[1]);
  not not_3 (not_3_out, Op[2]);
  and and_1 (and_1_out, not_1_out, not_2_out, not_3_out, not_4_out, not_5_out, Op[3]);
  not not_4 (not_4_out, Op[4]);
  not not_5 (not_5_out, Op[5]);
  and and_2 (and_2_out, ALUOp[1], not_6_out);
  not not_6 (not_6_out, ALUOp[0]);
  and and_3 (jr, and_1_out, and_2_out);
endmodule

module Shift_left_2 (
  input  [31:0] i32,
  output [31:0] o32
);


  assign o32 = {i32[29:0], 2'b00};
endmodule

module Shift_left_2_28 (
  input  [25:0] in26,
  output [27:0] out28
);


  assign out28 = {in26, 2'b00};
endmodule

module Sign_extend (
  input  [15:0] in16,
  output [31:0] out32
);


  assign out32 = {{16{1'b0}}, in16};
endmodule

module division_4 (
  input  [31:0] i,
  output [23:0] o
);


  assign o = i[25:2];
endmodule

module J (
  input  [27:0] in28,
  input  [3:0] in4,
  output [31:0] out32
);


  assign out32 = {in4, in28};
endmodule

module Stop (
  input  [31:0] Ins,
  output out_2
);

  wire or_1_out;

  or or_1 (or_1_out, Ins[0], Ins[1], Ins[2], Ins[3], Ins[4], Ins[5], Ins[6], Ins[7], Ins[8], Ins[9], Ins[10], Ins[11], Ins[12], Ins[13], Ins[14], Ins[15], Ins[17], Ins[18], Ins[19], Ins[20], Ins[21], Ins[22], Ins[23], Ins[24], Ins[25], Ins[26], Ins[27], Ins[28], Ins[29], Ins[30], Ins[31], Ins[16]);
  not not_1 (out_2, or_1_out);
endmodule

module ok (
  input  in_1,
  input  [31:0] in_2,
  output [23:0] out_3,
  output [23:0] out_4
);

  wire clk;
  wire [31:0] adder_1_out, register_1_q;

  Clock clock_1 (.out(clk));
  Register #(.width(32)) register_1 (.D(adder_1_out), .en(1'b1), .clk(clk), .Q(register_1_q), .clr(in_1));
  // Probe on register_1_q
  Adder #(.width(32)) adder_1 (.a(32'h4), .b(register_1_q), .out(adder_1_out));  // open: cin, cout
  division_4 division_4_1 (.i(in_2), .o(out_3));
  Bit_Extender #(.in_width(32), .out_width(24)) bit_extender_1 (.in(in_2), .out(out_4));

  // Other names for the same wires on the sheet: reset = in_1
endmodule
