// Logisim project SingleCycle_CPU.circ as structural Verilog
module Reg_File (
  input  CLK,
  input  Reset,
  input  [4:0] Read_Reg_1,
  input  [4:0] Read_Reg_2,
  input  [31:0] Write_Data,
  input  [4:0] Write_Reg,
  input  RegWrite,
  output [31:0] Read_Data_1,
  output [31:0] Read_Data_2
);

  wire S0, S1, S2, S3, S4, S5, S6, S7, S8, S9, S10, S11, S12, S13, S14, S15, S16, S17, S18, S19, S20, S21,
       S22, S23, S24, S25, S26, S27, S28, S29, S30, S31;
  wire [31:0] R0, R1, R2, R3, R4, R5, R6, R7, R8, R9, R10, R11, R12, R13, R14, R15, R16, R17, R18, R19, R20,
       R21, R22, R23, R24, R25, R26, R27, R28, R29, R30, R31;

  Register #(.width(32)) u_R0 (.D({32{1'b0}}), .en(S0), .clk(CLK), .Q(R0), .clr(Reset));
  Register #(.width(32)) u_R8 (.D(Write_Data), .en(S8), .clk(CLK), .Q(R8), .clr(Reset));
  Register #(.width(32)) u_R16 (.D(Write_Data), .en(S16), .clk(CLK), .Q(R16), .clr(Reset));
  Register #(.width(32)) u_R24 (.D(Write_Data), .en(S24), .clk(CLK), .Q(R24), .clr(Reset));
  Multiplexer #(.select(5), .width(32), .enable("false")) multiplexer_1 (
    .in0(R0), .in1(R1), .in2(R2), .in3(R3), .in4(R4), .in5(R5), .in6(R6), .in7(R7), .in8(R8), .in9(R9),
    .in10(R10), .in11(R11), .in12(R12), .in13(R13), .in14(R14), .in15(R15), .in16(R16), .in17(R17),
    .in18(R18), .in19(R19), .in20(R20), .in21(R21), .in22(R22), .in23(R23), .in24(R24), .in25(R25),
    .in26(R26), .in27(R27), .in28(R28), .in29(R29), .in30(R30), .in31(R31), .out(Read_Data_1),
    .sel(Read_Reg_1));
  Register #(.width(32)) u_R1 (.D(Write_Data), .en(S1), .clk(CLK), .Q(R1), .clr(Reset));
  Register #(.width(32)) u_R9 (.D(Write_Data), .en(S9), .clk(CLK), .Q(R9), .clr(Reset));
  Register #(.width(32)) u_R17 (.D(Write_Data), .en(S17), .clk(CLK), .Q(R17), .clr(Reset));
  Register #(.width(32)) u_R25 (.D(Write_Data), .en(S25), .clk(CLK), .Q(R25), .clr(Reset));
  Decoder #(.select(5)) decoder_1 (
    .out0(S0), .out1(S1), .out2(S2), .out3(S3), .out4(S4), .out5(S5), .out6(S6), .out7(S7), .out8(S8),
    .out9(S9), .out10(S10), .out11(S11), .out12(S12), .out13(S13), .out14(S14), .out15(S15), .out16(S16),
    .out17(S17), .out18(S18), .out19(S19), .out20(S20), .out21(S21), .out22(S22), .out23(S23), .out24(S24),
    .out25(S25), .out26(S26), .out27(S27), .out28(S28), .out29(S29), .out30(S30), .out31(S31),
    .sel(Write_Reg), .en(RegWrite));
  Register #(.width(32)) u_R2 (.D(Write_Data), .en(S2), .clk(CLK), .Q(R2), .clr(Reset));
  Register #(.width(32)) u_R10 (.D(Write_Data), .en(S10), .clk(CLK), .Q(R10), .clr(Reset));
  Register #(.width(32)) u_R18 (.D(Write_Data), .en(S18), .clk(CLK), .Q(R18), .clr(Reset));
  Register #(.width(32)) u_R26 (.D(Write_Data), .en(S26), .clk(CLK), .Q(R26), .clr(Reset));
  Register #(.width(32)) u_R3 (.D(Write_Data), .en(S3), .clk(CLK), .Q(R3), .clr(Reset));
  Register #(.width(32)) u_R11 (.D(Write_Data), .en(S11), .clk(CLK), .Q(R11), .clr(Reset));
  Register #(.width(32)) u_R19 (.D(Write_Data), .en(S19), .clk(CLK), .Q(R19), .clr(Reset));
  Register #(.width(32)) u_R27 (.D(Write_Data), .en(S27), .clk(CLK), .Q(R27), .clr(Reset));
  Register #(.width(32)) u_R4 (.D(Write_Data), .en(S4), .clk(CLK), .Q(R4), .clr(Reset));
  Register #(.width(32)) u_R12 (.D(Write_Data), .en(S12), .clk(CLK), .Q(R12), .clr(Reset));
  Register #(.width(32)) u_R20 (.D(Write_Data), .en(S20), .clk(CLK), .Q(R20), .clr(Reset));
  Register #(.width(32)) u_R28 (.D(Write_Data), .en(S28), .clk(CLK), .Q(R28), .clr(Reset));
  Register #(.width(32)) u_R5 (.D(Write_Data), .en(S5), .clk(CLK), .Q(R5), .clr(Reset));
  Register #(.width(32)) u_R13 (.D(Write_Data), .en(S13), .clk(CLK), .Q(R13), .clr(Reset));
  Register #(.width(32)) u_R21 (.D(Write_Data), .en(S21), .clk(CLK), .Q(R21), .clr(Reset));
  Register #(.width(32)) u_R29 (.D(Write_Data), .en(S29), .clk(CLK), .Q(R29), .clr(Reset));
  Register #(.width(32)) u_R6 (.D(Write_Data), .en(S6), .clk(CLK), .Q(R6), .clr(Reset));
  Register #(.width(32)) u_R14 (.D(Write_Data), .en(S14), .clk(CLK), .Q(R14), .clr(Reset));
  Register #(.width(32)) u_R22 (.D(Write_Data), .en(S22), .clk(CLK), .Q(R22), .clr(Reset));
  Register #(.width(32)) u_R30 (.D(Write_Data), .en(S30), .clk(CLK), .Q(R30), .clr(Reset));
  Multiplexer #(.select(5), .width(32), .enable("false")) multiplexer_2 (
    .in0(R0), .in1(R1), .in2(R2), .in3(R3), .in4(R4), .in5(R5), .in6(R6), .in7(R7), .in8(R8), .in9(R9),
    .in10(R10), .in11(R11), .in12(R12), .in13(R13), .in14(R14), .in15(R15), .in16(R16), .in17(R17),
    .in18(R18), .in19(R19), .in20(R20), .in21(R21), .in22(R22), .in23(R23), .in24(R24), .in25(R25),
    .in26(R26), .in27(R27), .in28(R28), .in29(R29), .in30(R30), .in31(R31), .out(Read_Data_2),
    .sel(Read_Reg_2));
  Register #(.width(32)) u_R7 (.D(Write_Data), .en(S7), .clk(CLK), .Q(R7), .clr(Reset));
  Register #(.width(32)) u_R15 (.D(Write_Data), .en(S15), .clk(CLK), .Q(R15), .clr(Reset));
  Register #(.width(32)) u_R23 (.D(Write_Data), .en(S23), .clk(CLK), .Q(R23), .clr(Reset));
  Register #(.width(32)) u_R31 (.D(Write_Data), .en(S31), .clk(CLK), .Q(R31), .clr(Reset));

  // Other names for the same wires on the sheet: ReadR1[4:0] = Read_Reg_1; ReadR2[4:0] = Read_Reg_2;
  //   WD[31:0] = Write_Data

  // Notes on the sheet:
  //   BANCO DE REGISTROS
endmodule
